// Logisim project RISC-V.circ as structural Verilog: 14 circuits, main circuit main
module main (
  input  Reset_PC,
  output [1:0] out_2,
  output [31:0] x3_output
);

  wire and_1_out, branch_1_branch_out, clock_1_out, clock_2_out, clock_3_out, control_unit_1_branch,
       control_unit_1_mem2reg, control_unit_1_operand_b, control_unit_1_register_write, control_unit_1_store,
       or_1_out, undriven;
  wire [1:0] control_unit_1_immediate_selector, control_unit_1_operand_a_select;
  wire [2:0] rom_1_data_2;
  wire [3:0] control_unit_1_alu_operation_selector;
  wire [31:0] adder_1_out, adder_2_out, alu_1_alu_out, I, immed_generation_1_s_imm, immed_generation_1_u_imm,
       multiplexer_1_out, multiplexer_2_out, multiplexer_3_out, multiplexer_4_out, multiplexer_5_out,
       ram_1_data, register_1_q, rom_1_data, rs1, rs2, SB, uj, write_back;

  Multiplexer #(.select(2), .width(32)) multiplexer_1 (
    .in0(adder_1_out), .in1(uj), .in2(adder_2_out), .in3(multiplexer_2_out), .out(multiplexer_1_out),
    .sel(out_2));  // open: en
  Register_part #(.width(32)) register_1 (
    .D(multiplexer_1_out), .Q(register_1_q), .clk(clock_1_out), .clr(Reset_PC));  // open: en
  Clock clock_1 (.out(clock_1_out));
  Branch branch_1 (.RS1(rs1), .Fun3(rom_1_data_2), .RS2(rs2), .Branch_Out(branch_1_branch_out));
  Adder #(.width(32)) adder_1 (.a(register_1_q), .b(32'h4), .out(adder_1_out));  // open: cin, cout
  Clock clock_2 (.out(clock_2_out));
  Multiplexer #(.width(32)) multiplexer_2 (
    .in0(adder_1_out), .in1(SB), .out(multiplexer_2_out), .sel(and_1_out));  // open: en
  ROM #(.addrWidth(12), .dataWidth(32)) rom_1 (
    .addr(register_1_q[13:2]), .data({rom_1_data[31:15], rom_1_data_2, rom_1_data[11:0]}));  // open: sel
  Immed__Generation immed_generation_1 (
    .i_imm(I), .s_imm(immed_generation_1_s_imm), .sb_imm(SB), .uj_imm(uj), .u_imm(immed_generation_1_u_imm),
    .PC(register_1_q), .INS({rom_1_data[31:15], rom_1_data_2, rom_1_data[11:0]}));
  and and_1 (and_1_out, control_unit_1_branch, branch_1_branch_out);
  Multiplexer #(.select(2), .width(32)) multiplexer_3 (
    .in0(I), .in1(immed_generation_1_s_imm), .in2(immed_generation_1_u_imm), .out(multiplexer_3_out),
    .sel(control_unit_1_immediate_selector), .en(undriven));  // open: in3
  Register register_2 (
    .WD1_Enable(control_unit_1_register_write), .WD1_Select(rom_1_data[11:7]), .Rs1_Out(rs1),
    .Rs1_Selector(rom_1_data[19:15]), .Rs2_Out(rs2), .Rs2_Selector(rom_1_data[24:20]), .Data_In(write_back),
    .x3(x3_output), .clock(clock_2_out));
  Control_Unit control_unit_1 (
    .Opcode_in(rom_1_data[6:0]), .Register_Write(control_unit_1_register_write),
    .Branch(control_unit_1_branch), .Store(control_unit_1_store), .mem2reg(control_unit_1_mem2reg),
    .Operand_A_select(control_unit_1_operand_a_select), .Operand_B(control_unit_1_operand_b),
    .Immediate_Selector(control_unit_1_immediate_selector), .Next_Pc(out_2), .Func3_input(rom_1_data_2),
    .Func7_input(rom_1_data[30]), .ALU_Operation_Selector(control_unit_1_alu_operation_selector));
  Multiplexer #(.select(2), .width(32)) multiplexer_4 (
    .in0(rs1), .in1(register_1_q), .in2(adder_1_out), .in3({32{1'b0}}), .out(multiplexer_4_out),
    .sel(control_unit_1_operand_a_select));  // open: en
  Multiplexer #(.width(32)) multiplexer_5 (
    .in0(rs2), .in1(multiplexer_3_out), .out(multiplexer_5_out), .sel(control_unit_1_operand_b));  // open: en
  ALU alu_1 (
    .Operand_A(multiplexer_4_out), .Operand_B(multiplexer_5_out),
    .Alu_Out_Select(control_unit_1_alu_operation_selector), .ALU_out(alu_1_alu_out));  // open: Overflow
  Adder #(.width(32)) adder_2 (.a(rs1), .b(I), .out(adder_2_out));  // open: cin, cout
  or or_1 (or_1_out, control_unit_1_store, control_unit_1_mem2reg);
  Clock clock_3 (.out(clock_3_out));
  RAM #(.addrWidth(12), .dataWidth(32), .bus("separate")) ram_1 (
    .addr(alu_1_alu_out[13:2]), .din(rs2), .data(ram_1_data), .str(control_unit_1_store), .sel(or_1_out),
    .clk(clock_3_out), .ld(control_unit_1_mem2reg));  // open: clr
  Multiplexer #(.width(32)) multiplexer_6 (
    .in0(alu_1_alu_out), .in1(ram_1_data), .out(write_back), .sel(control_unit_1_mem2reg));  // open: en

  // Notes on the sheet:
  //   contents of rom_1 (hex, n*v repeats v):
  //   5000113 193 213 100293 400313 393 a00413 100493 274d263 5201b3 500233 3002b3 332023 9383b3 fe83c4e3
  //   13 c0006f 9001b3 34000e7 67
  //   RV32i Single Cycle by Maaz Siddiqui
endmodule

// TYPE DECODE
module Type_decoder (
  input  [6:0] Opcode,
  output R,
  output I,
  output I__LOAD,
  output I__JALR,
  output S,
  output SB,
  output U__AUIPC,
  output U__LUI,
  output UJ__JAL
);

  wire comparator_1_eq, comparator_2_eq, comparator_3_lt;

  Comparator #(.width(7)) comparator_1 (.a(Opcode), .b(7'b0110011), .eq(comparator_1_eq));  // open: gt, lt
  Comparator #(.width(7)) comparator_2 (.a(Opcode), .b(7'b0111011), .eq(comparator_2_eq));  // open: gt, lt
  Comparator #(.width(7)) comparator_3 (.a(Opcode), .b(7'b0010011), .eq(I), .lt(comparator_3_lt));  // open: gt
  Comparator #(.width(7)) comparator_4 (.a(Opcode), .b(7'b0100011), .eq(S));  // open: gt, lt
  Comparator #(.width(7)) comparator_5 (.a(Opcode), .b(7'b1100011), .eq(SB));  // open: gt, lt
  Comparator #(.width(7)) comparator_6 (.a(Opcode), .b(7'b0010111), .eq(U__AUIPC));  // open: gt, lt
  Comparator #(.width(7)) comparator_7 (.a(Opcode), .b(7'b1101111), .eq(UJ__JAL));  // open: gt, lt
  or or_1 (R, comparator_1_eq, comparator_2_eq);
  Comparator #(.width(7)) comparator_8 (.a(Opcode), .b(7'b0000011), .eq(I__LOAD));  // open: gt, lt
  Comparator #(.width(7)) comparator_9 (.a(Opcode), .b(7'b0110111), .eq(U__LUI));  // open: gt, lt
  Comparator #(.width(7)) comparator_10 (.a(Opcode), .b(7'b1100111), .eq(I__JALR));  // open: gt, lt

  // Notes on the sheet:
  //   R-type
  //   R-type
  //   I -type
  //   S-type
  //   SB - type
  //   U -t ype
  //   UJ - type
endmodule

module Immed__Generation (
  input  [31:0] PC,
  input  [31:0] INS,
  output [31:0] i_imm,
  output [31:0] s_imm,
  output [31:0] sb_imm,
  output [31:0] uj_imm,
  output [31:0] u_imm
);

  wire [31:0] bit_extender_3_out, bit_extender_4_out, bit_extender_5_out;

  assign i_imm = {{20{INS[31]}}, INS[31:20]};  // Bit_Extender bit_extender_1
  assign s_imm = {{20{INS[31]}}, {INS[31:25], INS[11:7]}};  // Bit_Extender bit_extender_2
  assign bit_extender_3_out = {{19{INS[31]}}, {INS[31], INS[7], INS[30:25], INS[11:8], 1'b0}};  // Bit_Extender bit_extender_3
  assign bit_extender_4_out = {{11{INS[31]}}, {INS[31], INS[19:12], INS[20], INS[30:21], 1'b0}};  // Bit_Extender bit_extender_4
  assign bit_extender_5_out = {{12{1'b0}}, INS[31:12]};  // Bit_Extender bit_extender_5
  Adder #(.width(32)) adder_1 (.a(bit_extender_3_out), .b(PC), .out(sb_imm));  // open: cin, cout
  Adder #(.width(32)) adder_2 (.a(bit_extender_4_out), .b(PC), .out(uj_imm));  // open: cin, cout
  Shifter #(.width(32)) shifter_1 (.in(bit_extender_5_out), .\dist (5'b01100), .out(u_imm));
endmodule

module Register (
  input  [31:0] Data_In,
  input  WD1_Enable,
  input  [4:0] Rs1_Selector,
  input  [4:0] WD1_Select,
  input  [4:0] Rs2_Selector,
  input  clock,
  output [31:0] x3,
  output [31:0] Rs1_Out,
  output [31:0] Rs2_Out
);

  wire decoder_1_out0, decoder_1_out1, decoder_1_out2, decoder_1_out3, decoder_1_out4, decoder_1_out5,
       decoder_1_out6, decoder_1_out7, decoder_1_out8, decoder_1_out9, decoder_1_out10, decoder_1_out11,
       decoder_1_out12, decoder_1_out13, decoder_1_out14, decoder_1_out15, decoder_1_out16, decoder_1_out17,
       decoder_1_out18, decoder_1_out19, decoder_1_out20, decoder_1_out21, decoder_1_out22, decoder_1_out23,
       decoder_1_out24, decoder_1_out25, decoder_1_out26, decoder_1_out27, decoder_1_out28, decoder_1_out29,
       decoder_1_out30, decoder_1_out31;
  wire [31:0] x1, x2, x4, x5, x6, x7, x8, x9, x10, x11, x12, x13, x14, x15, x16, x17, x18, x19, x20, x21,
       x22, x23, x24, x25, x26, x27, x28, x29, x30, x31;

  Decoder #(.select(5), .disabled(0)) decoder_1 (
    .out0(decoder_1_out0), .out1(decoder_1_out1), .out2(decoder_1_out2), .out3(decoder_1_out3),
    .out4(decoder_1_out4), .out5(decoder_1_out5), .out6(decoder_1_out6), .out7(decoder_1_out7),
    .out8(decoder_1_out8), .out9(decoder_1_out9), .out10(decoder_1_out10), .out11(decoder_1_out11),
    .out12(decoder_1_out12), .out13(decoder_1_out13), .out14(decoder_1_out14), .out15(decoder_1_out15),
    .out16(decoder_1_out16), .out17(decoder_1_out17), .out18(decoder_1_out18), .out19(decoder_1_out19),
    .out20(decoder_1_out20), .out21(decoder_1_out21), .out22(decoder_1_out22), .out23(decoder_1_out23),
    .out24(decoder_1_out24), .out25(decoder_1_out25), .out26(decoder_1_out26), .out27(decoder_1_out27),
    .out28(decoder_1_out28), .out29(decoder_1_out29), .out30(decoder_1_out30), .out31(decoder_1_out31),
    .sel(WD1_Select), .en(WD1_Enable));
  Register_part #(.width(32)) register_1 (.D(Data_In), .en(decoder_1_out1), .Q(x1), .clk(clock));  // open: clr
  Register_part #(.width(32)) register_2 (.D(Data_In), .en(decoder_1_out2), .Q(x2), .clk(clock));  // open: clr
  Register_part #(.width(32)) register_3 (.D(Data_In), .en(decoder_1_out3), .Q(x3), .clk(clock));  // open: clr
  Register_part #(.width(32)) register_4 (.D(Data_In), .en(decoder_1_out4), .Q(x4), .clk(clock));  // open: clr
  Register_part #(.width(32)) register_5 (.D(Data_In), .en(decoder_1_out5), .Q(x5), .clk(clock));  // open: clr
  Register_part #(.width(32)) register_6 (.D(Data_In), .en(decoder_1_out6), .Q(x6), .clk(clock));  // open: clr
  Register_part #(.width(32)) register_7 (.D(Data_In), .en(decoder_1_out7), .Q(x7), .clk(clock));  // open: clr
  Register_part #(.width(32)) register_8 (.D(Data_In), .en(decoder_1_out8), .Q(x8), .clk(clock));  // open: clr
  Register_part #(.width(32)) register_9 (.D(Data_In), .en(decoder_1_out9), .Q(x9), .clk(clock));  // open: clr
  Register_part #(.width(32)) register_10 (.D(Data_In), .en(decoder_1_out10), .Q(x10), .clk(clock));  // open: clr
  Register_part #(.width(32)) register_11 (.D(Data_In), .en(decoder_1_out11), .Q(x11), .clk(clock));  // open: clr
  Register_part #(.width(32)) register_12 (.D(Data_In), .en(decoder_1_out12), .Q(x12), .clk(clock));  // open: clr
  Register_part #(.width(32)) register_13 (.D(Data_In), .en(decoder_1_out13), .Q(x13), .clk(clock));  // open: clr
  Register_part #(.width(32)) register_14 (.D(Data_In), .en(decoder_1_out14), .Q(x14), .clk(clock));  // open: clr
  Register_part #(.width(32)) register_15 (.D(Data_In), .en(decoder_1_out15), .Q(x15), .clk(clock));  // open: clr
  Register_part #(.width(32)) register_16 (.D(Data_In), .en(decoder_1_out16), .Q(x16), .clk(clock));  // open: clr
  Register_part #(.width(32)) register_17 (.D(Data_In), .en(decoder_1_out17), .Q(x17), .clk(clock));  // open: clr
  Register_part #(.width(32)) register_18 (.D(Data_In), .en(decoder_1_out18), .Q(x18), .clk(clock));  // open: clr
  Register_part #(.width(32)) register_19 (.D(Data_In), .en(decoder_1_out19), .Q(x19), .clk(clock));  // open: clr
  Register_part #(.width(32)) register_20 (.D(Data_In), .en(decoder_1_out20), .Q(x20), .clk(clock));  // open: clr
  Register_part #(.width(32)) register_21 (.D(Data_In), .en(decoder_1_out21), .Q(x21), .clk(clock));  // open: clr
  Register_part #(.width(32)) register_22 (.D(Data_In), .en(decoder_1_out22), .Q(x22), .clk(clock));  // open: clr
  Register_part #(.width(32)) register_23 (.D(Data_In), .en(decoder_1_out23), .Q(x23), .clk(clock));  // open: clr
  Register_part #(.width(32)) register_24 (.D(Data_In), .en(decoder_1_out24), .Q(x24), .clk(clock));  // open: clr
  Register_part #(.width(32)) register_25 (.D(Data_In), .en(decoder_1_out25), .Q(x25), .clk(clock));  // open: clr
  Register_part #(.width(32)) register_26 (.D(Data_In), .en(decoder_1_out26), .Q(x26), .clk(clock));  // open: clr
  Register_part #(.width(32)) register_27 (.D(Data_In), .en(decoder_1_out27), .Q(x27), .clk(clock));  // open: clr
  Register_part #(.width(32)) register_28 (.D(Data_In), .en(decoder_1_out28), .Q(x28), .clk(clock));  // open: clr
  Register_part #(.width(32)) register_29 (.D(Data_In), .en(decoder_1_out29), .Q(x29), .clk(clock));  // open: clr
  Register_part #(.width(32)) register_30 (.D(Data_In), .en(decoder_1_out30), .Q(x30), .clk(clock));  // open: clr
  Register_part #(.width(32)) register_31 (.D(Data_In), .en(decoder_1_out31), .Q(x31), .clk(clock));  // open: clr
  Multiplexer #(.select(5), .width(32)) multiplexer_1 (
    .in0({32{1'b0}}), .in1(x1), .in2(x2), .in3(x3), .in4(x4), .in5(x5), .in6(x6), .in7(x7), .in8(x8),
    .in9(x9), .in10(x10), .in11(x11), .in12(x12), .in13(x13), .in14(x14), .in15(x15), .in16(x16), .in17(x17),
    .in18(x18), .in19(x19), .in20(x20), .in21(x21), .in22(x22), .in23(x23), .in24(x24), .in25(x25),
    .in26(x26), .in27(x27), .in28(x28), .in29(x29), .in30(x30), .in31(x31), .out(Rs1_Out), .sel(Rs1_Selector));  // open: en
  Multiplexer #(.select(5), .width(32)) multiplexer_2 (
    .in0({32{1'b0}}), .in1(x1), .in2(x2), .in3(x3), .in4(x4), .in5(x5), .in6(x6), .in7(x7), .in8(x8),
    .in9(x9), .in10(x10), .in11(x11), .in12(x12), .in13(x13), .in14(x14), .in15(x15), .in16(x16), .in17(x17),
    .in18(x18), .in19(x19), .in20(x20), .in21(x21), .in22(x22), .in23(x23), .in24(x24), .in25(x25),
    .in26(x26), .in27(x27), .in28(x28), .in29(x29), .in30(x30), .in31(x31), .out(Rs2_Out), .sel(Rs2_Selector));  // open: en
endmodule

module Control_Decode (
  input  R_Type,
  input  I_Type,
  input  Load,
  input  JALR,
  input  Store,
  input  Branch,
  input  Auipc,
  input  Lui,
  input  JAL,
  input  [2:0] Fun3_input,
  input  Fun7_Input,
  output REG_Write,
  output Branch_2,
  output Store_2,
  output Mem_2_Reg,
  output [1:0] Operand_A,
  output Operand_B,
  output [1:0] IMM_SELECTOR,
  output [1:0] NEXT_PC,
  output [3:0] ALU_Operation_Selector_4_bit
);

  wire or_1_out, or_2_out, or_3_out;
  wire [2:0] type_to_3_bit_1_c;

  or or_1 (or_1_out, R_Type, I_Type, Load, JALR, Store, Branch);
  or or_2 (or_2_out, Auipc, Lui);
  or or_3 (or_3_out, JALR, JAL);
  or or_4 (REG_Write, I_Type, Load, JALR, R_Type, Auipc, Lui, JAL);
  Operend_A__select operend_a_select_1 (
    .jalr(or_3_out), .auipc(Auipc), .rsi(or_1_out), .zero(1'b0), .out0(Operand_A[1]), .out1(Operand_A[0]));
  or or_5 (Operand_B, I_Type, JALR, or_2_out, Store);
  Imm__Selector imm_selector_1 (
    .STYPE(Store), .UTYPE(or_2_out), .IType(I_Type), .a(IMM_SELECTOR[1]), .b(IMM_SELECTOR[0]));
  NEXT_PC_SELECT next_pc_select_1 (.SBTYPE(Branch), .JALR(JALR), .JAL(JAL), .a(NEXT_PC[1]), .b(NEXT_PC[0]));
  Type_to_3_bit type_to_3_bit_1 (
    .Rtype(R_Type), .itype(I_Type), .load(Load), .jalr(JALR), .store(Store), .auipc(Auipc), .lui(Lui),
    .jal(JAL), .a(type_to_3_bit_1_c[2]), .b(type_to_3_bit_1_c[1]), .c(type_to_3_bit_1_c[0]));
  ALU_Operation_4bit_selector alu_operation_4bit_selector_1 (
    .type_3bit_2(type_to_3_bit_1_c[2]), .type_3bit_1(type_to_3_bit_1_c[1]),
    .type_3bit_0(type_to_3_bit_1_c[0]), .fun3_2(Fun3_input[2]), .fun3_1(Fun3_input[1]),
    .fun3_0(Fun3_input[0]), .fun7_0(Fun7_Input), .AluOperation_0(ALU_Operation_Selector_4_bit[3]),
    .AluOperation_1(ALU_Operation_Selector_4_bit[2]), .AluOperation_2(ALU_Operation_Selector_4_bit[1]),
    .AluOperation_3(ALU_Operation_Selector_4_bit[0]));

  assign Branch_2 = Branch;
  assign Mem_2_Reg = Load;
  assign Store_2 = Store;
endmodule

module Operend_A__select (
  input  jalr,
  input  auipc,
  input  rsi,
  input  zero,
  output out0,
  output out1
);

  wire and_1_out, and_2_out, and_3_out, and_4_out, and_5_out, not_1_out, not_2_out, not_3_out, not_4_out,
       not_5_out, not_6_out, not_7_out, not_8_out, not_9_out, not_10_out, not_11_out, not_12_out, not_13_out,
       not_14_out;

  not not_1 (not_1_out, jalr);
  and and_1 (and_1_out, not_1_out, not_2_out, not_3_out);
  not not_2 (not_2_out, auipc);
  not not_3 (not_3_out, rsi);
  not not_4 (not_4_out, jalr);
  not not_5 (not_5_out, rsi);
  and and_2 (and_2_out, not_4_out, not_5_out, zero);
  not not_6 (not_6_out, jalr);
  and and_3 (and_3_out, not_6_out, not_7_out, not_8_out);
  not not_7 (not_7_out, auipc);
  not not_8 (not_8_out, rsi);
  not not_9 (not_9_out, jalr);
  not not_10 (not_10_out, rsi);
  and and_4 (and_4_out, not_9_out, not_10_out, not_11_out);
  not not_11 (not_11_out, zero);
  not not_12 (not_12_out, auipc);
  and and_5 (and_5_out, not_12_out, not_13_out, not_14_out);
  not not_13 (not_13_out, rsi);
  not not_14 (not_14_out, zero);
  or or_1 (out0, and_1_out, and_2_out);
  or or_2 (out1, and_3_out, and_4_out, and_5_out);
endmodule

module Imm__Selector (
  input  STYPE,
  input  UTYPE,
  input  IType,
  output a,
  output b
);

  wire not_1_out, not_2_out, not_3_out, not_4_out;

  not not_1 (not_1_out, STYPE);
  not not_2 (not_2_out, IType);
  not not_3 (not_3_out, UTYPE);
  not not_4 (not_4_out, IType);
  and and_1 (a, not_1_out, not_2_out);
  and and_2 (b, not_3_out, not_4_out);
endmodule

module NEXT_PC_SELECT (
  input  SBTYPE,
  input  JALR,
  input  JAL,
  output a,
  output b
);

  or or_1 (a, JALR, SBTYPE);
  or or_2 (b, JAL, SBTYPE);
endmodule

module ALU (
  input  [31:0] Operand_A,
  input  [31:0] Operand_B,
  input  [3:0] Alu_Out_Select,
  output Overflow,
  output [31:0] ALU_out
);

  wire comparator_1_lt, comparator_2_lt;
  wire [31:0] adder_1_out, and_1_out, bit_extender_1_out, bit_extender_2_out, or_1_out, shifter_1_out,
       shifter_2_out, shifter_3_out, subtractor_1_out, xor_1_out;

  Adder #(.width(32)) adder_1 (.a(Operand_A), .b(Operand_B), .out(adder_1_out), .cout(Overflow));  // open: cin
  Subtractor #(.width(32)) subtractor_1 (.a(Operand_A), .b(Operand_B), .out(subtractor_1_out));  // open: bin, bout
  Comparator #(.width(32)) comparator_1 (.a(Operand_A), .b(Operand_B), .lt(comparator_1_lt));  // open: gt, eq
  Comparator #(.width(32), .mode("unsigned")) comparator_2 (
    .a(Operand_A), .b(Operand_B), .lt(comparator_2_lt));  // open: gt, eq
  Shifter #(.width(32)) shifter_1 (.in(Operand_A), .\dist (Operand_B[4:0]), .out(shifter_1_out));
  assign xor_1_out = Operand_A ^ Operand_B;  // XOR_Gate xor_1, 32 bits wide
  assign and_1_out = Operand_A & Operand_B;  // AND_Gate and_1, 32 bits wide
  assign or_1_out = Operand_A | Operand_B;  // OR_Gate or_1, 32 bits wide
  Shifter #(.width(32), .shift("ar")) shifter_2 (.in(Operand_A), .\dist (Operand_B[4:0]), .out(shifter_2_out));
  Shifter #(.width(32), .shift("lr")) shifter_3 (.in(Operand_A), .\dist (Operand_B[4:0]), .out(shifter_3_out));
  assign bit_extender_1_out = {{31{1'b0}}, comparator_1_lt};  // Bit_Extender bit_extender_1
  assign bit_extender_2_out = {{31{1'b0}}, comparator_2_lt};  // Bit_Extender bit_extender_2
  Multiplexer #(.select(4), .width(32)) multiplexer_1 (
    .in0(adder_1_out), .in1(subtractor_1_out), .in2(and_1_out), .in3(or_1_out), .in4(xor_1_out),
    .in5(bit_extender_1_out), .in6(bit_extender_2_out), .in7(shifter_1_out), .in8(shifter_3_out),
    .in9(shifter_2_out), .in15(Operand_A), .out(ALU_out), .sel(Alu_Out_Select));  // open: in10, in11, in12, in13, in14, en
endmodule

module Type_to_3_bit (
  input  Rtype,
  input  itype,
  input  load,
  input  jalr,
  input  store,
  input  auipc,
  input  lui,
  input  jal,
  output a,
  output b,
  output c
);

  or or_1 (a, jal, lui, auipc, store);
  or or_2 (b, jal, lui, jalr, load);
  or or_3 (c, jal, auipc, jalr, itype);
endmodule

module ALU_Operation_4bit_selector (
  input  type_3bit_2,
  input  type_3bit_1,
  input  type_3bit_0,
  input  fun3_2,
  input  fun3_1,
  input  fun3_0,
  input  fun7_0,
  output AluOperation_0,
  output AluOperation_1,
  output AluOperation_2,
  output AluOperation_3
);

  wire and_1_out, and_2_out, and_3_out, and_4_out, and_5_out, and_6_out, and_7_out, and_8_out, and_9_out,
       and_10_out, and_11_out, and_12_out, and_13_out, and_14_out, and_15_out, and_16_out, and_17_out,
       and_18_out, and_19_out, and_20_out, not_1_out, not_2_out, not_3_out, not_4_out, not_5_out, not_6_out,
       not_7_out, not_8_out, not_9_out, not_10_out, not_11_out, not_12_out, not_13_out, not_14_out,
       not_15_out, not_16_out, not_17_out, not_18_out, not_19_out, not_20_out, not_21_out, not_22_out,
       not_23_out, not_24_out, not_25_out, not_26_out, not_27_out, not_28_out, not_29_out, not_30_out,
       not_31_out, not_32_out, not_33_out, not_34_out, not_35_out, not_36_out, not_37_out, not_38_out;

  not not_1 (not_1_out, type_3bit_2);
  not not_2 (not_2_out, fun3_1);
  not not_3 (not_3_out, type_3bit_2);
  not not_4 (not_4_out, type_3bit_2);
  not not_5 (not_5_out, type_3bit_1);
  not not_6 (not_6_out, fun3_2);
  not not_7 (not_7_out, type_3bit_2);
  not not_8 (not_8_out, type_3bit_0);
  not not_9 (not_9_out, type_3bit_2);
  not not_10 (not_10_out, type_3bit_1);
  not not_11 (not_11_out, fun3_1);
  not not_12 (not_12_out, fun3_0);
  not not_13 (not_13_out, fun7_0);
  not not_14 (not_14_out, type_3bit_2);
  not not_15 (not_15_out, fun3_1);
  not not_16 (not_16_out, fun3_0);
  not not_17 (not_17_out, type_3bit_2);
  not not_18 (not_18_out, fun3_2);
  not not_19 (not_19_out, type_3bit_2);
  not not_20 (not_20_out, type_3bit_0);
  not not_21 (not_21_out, fun3_0);
  not not_22 (not_22_out, type_3bit_2);
  not not_23 (not_23_out, fun3_0);
  not not_24 (not_24_out, type_3bit_2);
  not not_25 (not_25_out, type_3bit_2);
  not not_26 (not_26_out, type_3bit_2);
  not not_27 (not_27_out, type_3bit_0);
  not not_28 (not_28_out, fun3_1);
  not not_29 (not_29_out, type_3bit_2);
  not not_30 (not_30_out, fun3_2);
  not not_31 (not_31_out, fun3_1);
  not not_32 (not_32_out, type_3bit_2);
  not not_33 (not_33_out, fun3_1);
  not not_34 (not_34_out, type_3bit_2);
  not not_35 (not_35_out, type_3bit_1);
  not not_36 (not_36_out, fun3_0);
  and and_1 (and_1_out, not_1_out, fun3_2, not_2_out, fun3_0);
  and and_2 (and_2_out, not_3_out, type_3bit_1);
  and and_3 (and_3_out, type_3bit_1, type_3bit_0);
  not not_37 (not_37_out, type_3bit_2);
  not not_38 (not_38_out, fun3_2);
  and and_4 (and_4_out, not_37_out, not_38_out, fun3_0);
  and and_5 (and_5_out, not_4_out, not_5_out, not_6_out, fun3_1);
  and and_6 (and_6_out, not_7_out, not_8_out, fun3_1, fun3_0);
  and and_7 (and_7_out, not_9_out, not_10_out, fun3_2, not_11_out, not_12_out, not_13_out);
  and and_8 (and_8_out, not_14_out, type_3bit_0, fun3_2, not_15_out, not_16_out);
  and and_9 (and_9_out, type_3bit_1, type_3bit_0);
  and and_10 (and_10_out, not_17_out, not_18_out, fun3_0);
  and and_11 (and_11_out, not_19_out, not_20_out, fun3_2, not_21_out, fun7_0);
  and and_12 (and_12_out, not_22_out, fun3_2, fun3_1, not_23_out);
  and and_13 (and_13_out, not_24_out, type_3bit_0, fun3_1, fun3_0);
  and and_14 (and_14_out, not_25_out, type_3bit_1);
  and and_15 (and_15_out, type_3bit_1, type_3bit_0);
  and and_16 (and_16_out, not_26_out, not_27_out, not_28_out, fun7_0);
  and and_17 (and_17_out, not_29_out, not_30_out, not_31_out, fun3_0);
  and and_18 (and_18_out, not_32_out, not_33_out, fun3_0, fun7_0);
  and and_19 (and_19_out, not_34_out, not_35_out, fun3_1, not_36_out);
  and and_20 (and_20_out, type_3bit_1, type_3bit_0);
  or or_1 (AluOperation_0, and_1_out, and_2_out, and_3_out);
  or or_2 (AluOperation_2, and_10_out, and_11_out, and_12_out, and_13_out, and_14_out, and_15_out);
  or or_3 (AluOperation_3, and_16_out, and_17_out, and_18_out, and_19_out, and_20_out);
  or or_4 (AluOperation_1, and_4_out, and_5_out, and_6_out, and_7_out, and_8_out, and_9_out);
endmodule

module Control_Unit (
  input  [6:0] Opcode_in,
  input  [2:0] Func3_input,
  input  Func7_input,
  output Register_Write,
  output Branch,
  output Store,
  output mem2reg,
  output [1:0] Operand_A_select,
  output [3:0] ALU_Operation_Selector,
  output Operand_B,
  output [1:0] Immediate_Selector,
  output [1:0] Next_Pc
);

  wire type_decoder_1_i, type_decoder_1_i__jalr, type_decoder_1_i__load, type_decoder_1_r, type_decoder_1_s,
       type_decoder_1_sb, type_decoder_1_u__auipc, type_decoder_1_u__lui, type_decoder_1_uj__jal;

  Type_decoder type_decoder_1 (
    .R(type_decoder_1_r), .I(type_decoder_1_i), .I__LOAD(type_decoder_1_i__load),
    .I__JALR(type_decoder_1_i__jalr), .S(type_decoder_1_s), .SB(type_decoder_1_sb),
    .U__AUIPC(type_decoder_1_u__auipc), .U__LUI(type_decoder_1_u__lui), .UJ__JAL(type_decoder_1_uj__jal),
    .Opcode(Opcode_in));
  Control_Decode control_decode_1 (
    .REG_Write(Register_Write), .Branch_2(Branch), .Store_2(Store), .Mem_2_Reg(mem2reg),
    .Operand_A(Operand_A_select), .Operand_B(Operand_B), .IMM_SELECTOR(Immediate_Selector),
    .NEXT_PC(Next_Pc), .R_Type(type_decoder_1_r), .I_Type(type_decoder_1_i), .Load(type_decoder_1_i__load),
    .JALR(type_decoder_1_i__jalr), .Store(type_decoder_1_s), .Branch(type_decoder_1_sb),
    .Auipc(type_decoder_1_u__auipc), .Lui(type_decoder_1_u__lui), .JAL(type_decoder_1_uj__jal),
    .Fun3_input(Func3_input), .Fun7_Input(Func7_input), .ALU_Operation_Selector_4_bit(ALU_Operation_Selector));
endmodule

module PC (
  input  [11:0] currentPC,
  input  Reset_PC,
  output [6:0] Opcode,
  output [31:0] Instruction_Out
);

  wire clock_1_out;
  wire [31:0] adder_1_out, register_1_q;

  Register_part #(.width(32)) register_1 (
    .D(adder_1_out), .Q({register_1_q[31:14], currentPC, register_1_q[1:0]}), .clk(clock_1_out),
    .clr(Reset_PC));  // open: en
  Clock clock_1 (.out(clock_1_out));
  Adder #(.width(32)) adder_1 (
    .a({register_1_q[31:14], currentPC, register_1_q[1:0]}), .b(32'h4), .out(adder_1_out));  // open: cin, cout
  ROM #(.addrWidth(12), .dataWidth(32)) rom_1 (.addr(currentPC), .data(Instruction_Out));  // open: sel

  assign Opcode = Instruction_Out[6:0];

  // Notes on the sheet:
  //   contents of rom_1 (hex, n*v repeats v):
  //   a00513 108093 500293 130313 a31263 231213 1203b3 fea314e3
endmodule

module Branch (
  input  [31:0] RS1,
  input  [2:0] Fun3,
  input  [31:0] RS2,
  output Branch_Out
);

  wire comparator_1_eq, comparator_2_eq, comparator_3_lt, comparator_4_eq, comparator_4_gt, comparator_5_lt,
       comparator_6_eq, comparator_6_gt, not_1_out, or_1_out, or_2_out;

  Comparator #(.width(32)) comparator_1 (.a(RS1), .b(RS2), .eq(comparator_1_eq));  // open: gt, lt
  Comparator #(.width(32)) comparator_2 (.a(RS1), .b(RS2), .eq(comparator_2_eq));  // open: gt, lt
  Comparator #(.width(32)) comparator_3 (.a(RS1), .b(RS2), .lt(comparator_3_lt));  // open: gt, eq
  Comparator #(.width(32)) comparator_4 (.a(RS1), .b(RS2), .gt(comparator_4_gt), .eq(comparator_4_eq));  // open: lt
  Comparator #(.width(32), .mode("unsigned")) comparator_5 (.a(RS1), .b(RS2), .lt(comparator_5_lt));  // open: gt, eq
  Comparator #(.width(32), .mode("unsigned")) comparator_6 (
    .a(RS1), .b(RS2), .gt(comparator_6_gt), .eq(comparator_6_eq));  // open: lt
  not not_1 (not_1_out, comparator_2_eq);
  or or_1 (or_1_out, comparator_4_gt, comparator_4_eq);
  or or_2 (or_2_out, comparator_6_gt, comparator_6_eq);
  Multiplexer #(.select(3)) multiplexer_1 (
    .in0(comparator_1_eq), .in1(not_1_out), .in4(comparator_3_lt), .in5(or_1_out), .in6(comparator_5_lt),
    .in7(or_2_out), .out(Branch_Out), .sel(Fun3));  // open: in2, in3, en

  // Notes on the sheet:
  //   beq
  //   bne
  //   blt
  //   bge
  //   bltu
  //   bgeu
endmodule
